# Fritzing sketch Bluetooth_car (saved by Fritzing 0.9.3b)
breadboards: 1

parts:
  Part1 = Bluetooth HC-05 Macho
  Part2 = Arduino Nano (Rev3.0) (ICSP)
  R1 = Resistor [tolerance=±5% resistance=2.2k package="2010 [SMD]"]
  R2 = Resistor [tolerance=±5% resistance=4.7k package="0603 [SMD]"]
  LED1 = LED - 5mm [color="Red (633nm)" package="5 mm [THT]"]

nets:
  N1: Part1.TXD, Part2.D0/RX
  N2: Part1.RXD, R1.Pin_0
  VCC: Part1.VCC, Part2.5V
  GND: Part1.GND, Part2.GND, Part2.D7, R2.Pin_1, LED1.anode
  N3: Part2.D1/TX, R1.Pin_1, R2.Pin_0
  N4: Part2.D8, LED1.cathode

notes:
  Power Supply 12V
  To Motor Driver Inputs
